// Logisim project ramchip_selection_circuit.circ as structural Verilog: 1 circuit, main circuit main
module main (
  input  A13,
  input  A14,
  input  S0,
  input  S1,
  input  S2,
  output A13_2,
  output A14_2,
  output RAMC1,
  output RAMC2
);

  wire and_1_out, and_2_out, and_3_out, and_4_out, and_5_out, and_7_out, not_1_out, not_2_out, not_3_out,
       not_4_out, or_2_out;

  and and_1 (and_1_out, A14, S1);
  not not_1 (not_1_out, S1);
  and and_2 (and_2_out, A14, S2);
  and and_3 (and_3_out, A14, S1);
  not not_2 (not_2_out, S1);
  not not_3 (not_3_out, S2);
  and and_4 (and_4_out, and_1_out, S2);
  and and_5 (and_5_out, A14, S0);
  and and_6 (A14_2, A14, not_1_out);
  or or_1 (RAMC1, and_2_out, and_3_out);
  not not_4 (not_4_out, A14);
  and and_7 (and_7_out, not_2_out, not_3_out);
  or or_2 (or_2_out, and_4_out, and_5_out);
  or or_3 (RAMC2, not_4_out, and_7_out);
  or or_4 (A13_2, or_2_out, A13);
endmodule
